// Logisim project procesor.circ as structural Verilog: 11 circuits, main circuit main
module main (
  input  b1f,
  input  b1s,
  input  b2f,
  input  b2s,
  input  b3f,
  input  b3s,
  input  b4f,
  input  b4s,
  input  b5f,
  input  b5s,
  input  b6f,
  input  b6s,
  input  b7f,
  input  b7s,
  input  b8f,
  input  b8s,
  output out_17,
  output Equal
);

  wire and_1_out, and_2_out, and_3_out, and_4_out, and_5_out, and_7_out, compering_module_1_b1_is_greater,
       compering_module_1_b2_is_greater, compering_module_1_equal, compering_module_2_b1_is_greater,
       compering_module_2_b2_is_greater, compering_module_2_equal, compering_module_3_b1_is_greater,
       compering_module_3_b2_is_greater, compering_module_3_equal, compering_module_4_b1_is_greater,
       compering_module_4_b2_is_greater, compering_module_4_equal, compering_module_5_b1_is_greater,
       compering_module_5_b2_is_greater, compering_module_5_equal, compering_module_6_b1_is_greater,
       compering_module_6_b2_is_greater, compering_module_6_equal, compering_module_7_b1_is_greater,
       compering_module_7_b2_is_greater, compering_module_7_equal, compering_module_8_b1_is_greater,
       compering_module_8_equal;

  compering_module compering_module_1 (
    .B1(b1f), .B2(b1s), .B1_is_greater(compering_module_1_b1_is_greater),
    .B2_is_greater(compering_module_1_b2_is_greater), .Equal(compering_module_1_equal));
  compering_module compering_module_2 (
    .B1(b2f), .B2(b2s), .B1_is_greater(compering_module_2_b1_is_greater),
    .B2_is_greater(compering_module_2_b2_is_greater), .Equal(compering_module_2_equal));
  compering_module compering_module_3 (
    .B1(b3f), .B2(b3s), .B1_is_greater(compering_module_3_b1_is_greater),
    .B2_is_greater(compering_module_3_b2_is_greater), .Equal(compering_module_3_equal));
  compering_module compering_module_4 (
    .B1(b4f), .B2(b4s), .B1_is_greater(compering_module_4_b1_is_greater),
    .B2_is_greater(compering_module_4_b2_is_greater), .Equal(compering_module_4_equal));
  compering_module compering_module_5 (
    .B1(b5f), .B2(b5s), .B1_is_greater(compering_module_5_b1_is_greater),
    .B2_is_greater(compering_module_5_b2_is_greater), .Equal(compering_module_5_equal));
  compering_module compering_module_6 (
    .B1(b6f), .B2(b6s), .B1_is_greater(compering_module_6_b1_is_greater),
    .B2_is_greater(compering_module_6_b2_is_greater), .Equal(compering_module_6_equal));
  compering_module compering_module_7 (
    .B1(b7f), .B2(b7s), .B1_is_greater(compering_module_7_b1_is_greater),
    .B2_is_greater(compering_module_7_b2_is_greater), .Equal(compering_module_7_equal));
  compering_module compering_module_8 (
    .B1(b8f), .B2(b8s), .B1_is_greater(compering_module_8_b1_is_greater), .B2_is_greater(out_17),
    .Equal(compering_module_8_equal));
  and and_1 (and_1_out, compering_module_1_equal, compering_module_2_equal);
  and and_2 (and_2_out, compering_module_3_equal, compering_module_4_equal);
  and and_3 (and_3_out, compering_module_5_equal, compering_module_6_equal);
  and and_4 (and_4_out, compering_module_7_equal, compering_module_8_equal);
  and and_5 (and_5_out, and_1_out, and_2_out);
  and and_6 (Equal, and_5_out, and_7_out);
  and and_7 (and_7_out, and_3_out, and_4_out);
endmodule

module add_bits_of_1 (
);

  wire and_1_out, and_2_out, and_3_out, and_4_out, and_5_out, and_6_out, and_7_out, and_8_out, and_9_out,
       and_10_out, and_11_out, and_12_out, dipswitch_1_p1, dipswitch_1_p2, dipswitch_1_p3, dipswitch_1_p4,
       dipswitch_1_p5, dipswitch_1_p6, dipswitch_1_p7, dipswitch_1_p8, or_1_out, or_2_out, or_3_out,
       xor_1_out, xor_2_out, xor_3_out, xor_4_out, xor_5_out, xor_6_out, xor_7_out, xor_8_out, xor_9_out,
       xor_10_out, xor_11_out, xor_12_out, xor_13_out;

  // DipSwitch dipswitch_1: pin names not known; wires that end beside it: dipswitch_1_p1, dipswitch_1_p2, dipswitch_1_p3, dipswitch_1_p4, dipswitch_1_p5, dipswitch_1_p6, dipswitch_1_p7, dipswitch_1_p8
  and and_1 (and_1_out, dipswitch_1_p1, dipswitch_1_p2);
  and and_2 (and_2_out, dipswitch_1_p3, dipswitch_1_p4);
  and and_3 (and_3_out, dipswitch_1_p5, dipswitch_1_p6);
  and and_4 (and_4_out, dipswitch_1_p7, dipswitch_1_p8);
  xor xor_1 (xor_1_out, dipswitch_1_p1, dipswitch_1_p2);
  and and_5 (and_5_out, xor_1_out, xor_2_out);
  xor xor_2 (xor_2_out, dipswitch_1_p3, dipswitch_1_p4);
  and and_6 (and_6_out, and_1_out, and_2_out);
  xor xor_3 (xor_3_out, dipswitch_1_p5, dipswitch_1_p6);
  and and_7 (and_7_out, xor_3_out, xor_4_out);
  xor xor_4 (xor_4_out, dipswitch_1_p7, dipswitch_1_p8);
  and and_8 (and_8_out, and_3_out, and_4_out);
  xor xor_5 (xor_5_out, xor_1_out, xor_2_out);
  or or_1 (or_1_out, and_5_out, xor_6_out);
  xor xor_6 (xor_6_out, and_1_out, and_2_out);
  xor xor_7 (xor_7_out, xor_3_out, xor_4_out);
  or or_2 (or_2_out, and_7_out, xor_8_out);
  xor xor_8 (xor_8_out, and_3_out, and_4_out);
  xor xor_9 (xor_9_out, xor_5_out, xor_7_out);
  and and_9 (and_9_out, xor_5_out, xor_7_out);
  xor xor_10 (xor_10_out, or_1_out, or_2_out);
  and and_10 (and_10_out, or_1_out, or_2_out);
  xor xor_11 (xor_11_out, and_6_out, and_8_out);
  and and_11 (and_11_out, and_6_out, and_8_out);
  xor xor_12 (xor_12_out, and_9_out, xor_10_out);
  and and_12 (and_12_out, xor_10_out, and_9_out);
  xor xor_13 (xor_13_out, and_10_out, xor_11_out);
  LED led_1 (.in(xor_9_out));
  LED led_2 (.in(xor_12_out));
  or or_3 (or_3_out, and_12_out, xor_13_out);
  LED led_3 (.in(or_3_out));
  LED led_4 (.in(and_11_out));
endmodule

module xor_and (
  input  A,
  input  B,
  output XOR_r,
  output AND_r
);

  xor xor_1 (XOR_r, A, B);
  and and_1 (AND_r, A, B);
endmodule

module invert_8_inputs (
  input  b1,
  input  b2,
  input  b3,
  input  b4,
  input  b5,
  input  b6,
  input  b7,
  input  b8,
  output b8o,
  output b7o,
  output b6o,
  output b5o,
  output b4o,
  output b3o,
  output b2o,
  output b1o
);


  assign b1o = b1;
  assign b2o = b2;
  assign b3o = b3;
  assign b4o = b4;
  assign b5o = b5;
  assign b6o = b6;
  assign b7o = b7;
  assign b8o = b8;
endmodule

module adding_module (
  input  B1F,
  input  B3F,
  input  B5F,
  input  B7F,
  input  B1S,
  input  B3S,
  input  B5S,
  input  B7S,
  input  B2F,
  input  B4F,
  input  B6F,
  input  B8F,
  input  B2S,
  input  B4S,
  input  B6S,
  input  B8S,
  output B1O,
  output B3O,
  output B5O,
  output B7O,
  output ERROR,
  output B2O,
  output B4O,
  output B6O,
  output B8O
);

  wire xor_and_1_and_r, xor_and_1_xor_r, xor_and_2_and_r, xor_and_2_xor_r, xor_and_3_and_r, xor_and_3_xor_r,
       xor_and_4_and_r, xor_and_4_xor_r, xor_and_5_and_r, xor_and_5_xor_r, xor_and_6_and_r, xor_and_6_xor_r,
       xor_and_7_and_r, xor_and_7_xor_r, xor_and_8_and_r, xor_and_8_xor_r, xor_and_9_and_r, xor_and_9_xor_r,
       xor_and_10_xor_r, xor_and_11_and_r, xor_and_11_xor_r, xor_and_12_xor_r, xor_and_13_and_r,
       xor_and_13_xor_r, xor_and_14_and_r, xor_and_14_xor_r, xor_and_15_and_r, xor_and_15_xor_r,
       xor_and_16_and_r, xor_and_16_xor_r, xor_and_17_and_r, xor_and_17_xor_r, xor_and_18_and_r,
       xor_and_18_xor_r, xor_and_19_and_r, xor_and_19_xor_r, xor_and_20_and_r, xor_and_20_xor_r,
       xor_and_21_and_r, xor_and_21_xor_r, xor_and_22_and_r, xor_and_22_xor_r, xor_and_23_and_r,
       xor_and_23_xor_r, xor_and_24_and_r, xor_and_24_xor_r, xor_and_25_xor_r, xor_and_26_xor_r,
       xor_and_27_and_r, xor_and_27_xor_r, xor_and_28_xor_r, xor_and_29_and_r, xor_and_29_xor_r,
       xor_and_30_xor_r, xor_and_31_and_r, xor_and_31_xor_r, xor_and_32_and_r, xor_and_32_xor_r,
       xor_and_33_and_r, xor_and_33_xor_r, xor_and_34_and_r, xor_and_34_xor_r, xor_and_35_xor_r,
       xor_and_36_xor_r;

  xor_and xor_and_1 (.A(B1F), .B(B1S), .XOR_r(xor_and_1_xor_r), .AND_r(xor_and_1_and_r));
  xor_and xor_and_2 (.A(xor_and_3_and_r), .B(xor_and_17_xor_r), .XOR_r(xor_and_2_xor_r), .AND_r(xor_and_2_and_r));
  xor_and xor_and_3 (.A(xor_and_4_and_r), .B(xor_and_5_xor_r), .XOR_r(xor_and_3_xor_r), .AND_r(xor_and_3_and_r));
  xor_and xor_and_4 (.A(xor_and_7_and_r), .B(xor_and_6_xor_r), .XOR_r(xor_and_4_xor_r), .AND_r(xor_and_4_and_r));
  xor_and xor_and_5 (.A(xor_and_6_and_r), .B(xor_and_21_xor_r), .XOR_r(xor_and_5_xor_r), .AND_r(xor_and_5_and_r));
  xor_and xor_and_6 (.A(xor_and_8_and_r), .B(xor_and_9_xor_r), .XOR_r(xor_and_6_xor_r), .AND_r(xor_and_6_and_r));
  xor_and xor_and_7 (.A(xor_and_1_and_r), .B(xor_and_8_xor_r), .XOR_r(xor_and_7_xor_r), .AND_r(xor_and_7_and_r));
  xor_and xor_and_8 (.A(B2F), .B(B2S), .XOR_r(xor_and_8_xor_r), .AND_r(xor_and_8_and_r));
  xor_and xor_and_9 (.A(B3F), .B(B3S), .XOR_r(xor_and_9_xor_r), .AND_r(xor_and_9_and_r));
  xor_and xor_and_10 (.A(xor_and_11_and_r), .B(xor_and_12_xor_r), .XOR_r(xor_and_10_xor_r));  // open: AND_r
  xor_and xor_and_11 (.A(xor_and_13_and_r), .B(xor_and_14_xor_r), .XOR_r(xor_and_11_xor_r), .AND_r(xor_and_11_and_r));
  xor_and xor_and_12 (.A(xor_and_14_and_r), .B(xor_and_25_xor_r), .XOR_r(xor_and_12_xor_r));  // open: AND_r
  xor_and xor_and_13 (.A(xor_and_2_and_r), .B(xor_and_15_xor_r), .XOR_r(xor_and_13_xor_r), .AND_r(xor_and_13_and_r));
  xor_and xor_and_14 (.A(xor_and_15_and_r), .B(xor_and_16_xor_r), .XOR_r(xor_and_14_xor_r), .AND_r(xor_and_14_and_r));
  xor_and xor_and_15 (.A(xor_and_17_and_r), .B(xor_and_18_xor_r), .XOR_r(xor_and_15_xor_r), .AND_r(xor_and_15_and_r));
  xor_and xor_and_16 (.A(xor_and_18_and_r), .B(xor_and_27_xor_r), .XOR_r(xor_and_16_xor_r), .AND_r(xor_and_16_and_r));
  xor_and xor_and_17 (.A(xor_and_5_and_r), .B(xor_and_19_xor_r), .XOR_r(xor_and_17_xor_r), .AND_r(xor_and_17_and_r));
  xor_and xor_and_18 (.A(xor_and_19_and_r), .B(xor_and_20_xor_r), .XOR_r(xor_and_18_xor_r), .AND_r(xor_and_18_and_r));
  xor_and xor_and_19 (.A(xor_and_21_and_r), .B(xor_and_22_xor_r), .XOR_r(xor_and_19_xor_r), .AND_r(xor_and_19_and_r));
  xor_and xor_and_20 (.A(xor_and_22_and_r), .B(xor_and_31_xor_r), .XOR_r(xor_and_20_xor_r), .AND_r(xor_and_20_and_r));
  xor_and xor_and_21 (.A(xor_and_9_and_r), .B(xor_and_23_xor_r), .XOR_r(xor_and_21_xor_r), .AND_r(xor_and_21_and_r));
  xor_and xor_and_22 (.A(xor_and_23_and_r), .B(xor_and_24_xor_r), .XOR_r(xor_and_22_xor_r), .AND_r(xor_and_22_and_r));
  xor_and xor_and_23 (.A(B4F), .B(B4S), .XOR_r(xor_and_23_xor_r), .AND_r(xor_and_23_and_r));
  xor_and xor_and_24 (.A(B5F), .B(B5S), .XOR_r(xor_and_24_xor_r), .AND_r(xor_and_24_and_r));
  xor_and xor_and_25 (.A(xor_and_16_and_r), .B(xor_and_26_xor_r), .XOR_r(xor_and_25_xor_r));  // open: AND_r
  xor_and xor_and_26 (.A(xor_and_27_and_r), .B(xor_and_28_xor_r), .XOR_r(xor_and_26_xor_r));  // open: AND_r
  xor_and xor_and_27 (.A(xor_and_20_and_r), .B(xor_and_29_xor_r), .XOR_r(xor_and_27_xor_r), .AND_r(xor_and_27_and_r));
  xor_and xor_and_28 (.A(xor_and_29_and_r), .B(xor_and_30_xor_r), .XOR_r(xor_and_28_xor_r));  // open: AND_r
  xor_and xor_and_29 (.A(xor_and_31_and_r), .B(xor_and_32_xor_r), .XOR_r(xor_and_29_xor_r), .AND_r(xor_and_29_and_r));
  xor_and xor_and_30 (.A(xor_and_32_and_r), .B(xor_and_35_xor_r), .XOR_r(xor_and_30_xor_r));  // open: AND_r
  xor_and xor_and_31 (.A(xor_and_24_and_r), .B(xor_and_33_xor_r), .XOR_r(xor_and_31_xor_r), .AND_r(xor_and_31_and_r));
  xor_and xor_and_32 (.A(xor_and_33_and_r), .B(xor_and_34_xor_r), .XOR_r(xor_and_32_xor_r), .AND_r(xor_and_32_and_r));
  xor_and xor_and_33 (.A(B6F), .B(B6S), .XOR_r(xor_and_33_xor_r), .AND_r(xor_and_33_and_r));
  xor_and xor_and_34 (.A(B7F), .B(B7S), .XOR_r(xor_and_34_xor_r), .AND_r(xor_and_34_and_r));
  xor_and xor_and_35 (.A(xor_and_34_and_r), .B(xor_and_36_xor_r), .XOR_r(xor_and_35_xor_r));  // open: AND_r
  xor_and xor_and_36 (.A(B8F), .B(B8S), .XOR_r(xor_and_36_xor_r), .AND_r(ERROR));
  invert_8_inputs invert_8_inputs_1 (
    .b1(xor_and_1_xor_r), .b2(xor_and_7_xor_r), .b3(xor_and_4_xor_r), .b4(xor_and_3_xor_r),
    .b5(xor_and_2_xor_r), .b6(xor_and_13_xor_r), .b7(xor_and_11_xor_r), .b8(xor_and_10_xor_r), .b8o(B8O),
    .b7o(B7O), .b6o(B6O), .b5o(B5O), .b4o(B4O), .b3o(B3O), .b2o(B2O), .b1o(B1O));
endmodule

module multiy_component (
  input  Mno,
  input  b1,
  input  b2,
  input  b3,
  input  b4,
  input  b5,
  input  b6,
  input  b7,
  input  b8,
  output b1o,
  output b2o,
  output b3o,
  output b4o,
  output b5o,
  output b6o,
  output b7o,
  output b8o
);

  and and_1 (b1o, Mno, b1);
  and and_2 (b3o, Mno, b3);
  and and_3 (b4o, Mno, b4);
  and and_4 (b2o, Mno, b2);
  and and_5 (b5o, Mno, b5);
  and and_6 (b6o, Mno, b6);
  and and_7 (b7o, Mno, b7);
  and and_8 (b8o, Mno, b8);
endmodule

module adding_16_bit (
  input  in_1,
  input  in_2,
  input  in_3,
  input  in_4,
  input  in_5,
  input  in_6,
  input  in_7,
  input  in_8,
  input  in_9,
  input  in_10,
  input  in_11,
  input  in_12,
  input  in_13,
  input  in_14,
  input  in_15,
  input  in_16,
  input  in_17,
  input  in_18,
  input  in_19,
  input  in_20,
  input  in_21,
  input  in_22,
  input  in_23,
  input  in_24,
  input  in_25,
  input  in_26,
  input  in_27,
  input  in_28,
  input  in_29,
  input  in_30,
  input  in_31,
  input  in_32
);

  wire xor_and_1_and_r, xor_and_1_xor_r, xor_and_2_and_r, xor_and_2_xor_r, xor_and_3_and_r, xor_and_3_xor_r,
       xor_and_4_and_r, xor_and_4_xor_r, xor_and_5_and_r, xor_and_5_xor_r, xor_and_6_and_r, xor_and_6_xor_r,
       xor_and_7_and_r, xor_and_7_xor_r, xor_and_8_and_r, xor_and_8_xor_r, xor_and_9_and_r, xor_and_9_xor_r,
       xor_and_10_and_r, xor_and_10_xor_r, xor_and_11_and_r, xor_and_11_xor_r, xor_and_12_and_r,
       xor_and_12_xor_r, xor_and_13_and_r, xor_and_13_xor_r, xor_and_14_and_r, xor_and_14_xor_r,
       xor_and_15_and_r, xor_and_15_xor_r, xor_and_16_and_r, xor_and_16_xor_r, xor_and_17_and_r,
       xor_and_17_xor_r, xor_and_18_and_r, xor_and_18_xor_r, xor_and_19_xor_r, xor_and_20_and_r,
       xor_and_20_xor_r, xor_and_21_and_r, xor_and_21_xor_r, xor_and_22_and_r, xor_and_22_xor_r,
       xor_and_23_and_r, xor_and_23_xor_r, xor_and_24_and_r, xor_and_24_xor_r, xor_and_25_and_r,
       xor_and_25_xor_r, xor_and_26_and_r, xor_and_26_xor_r, xor_and_27_and_r, xor_and_27_xor_r,
       xor_and_28_and_r, xor_and_28_xor_r, xor_and_29_and_r, xor_and_29_xor_r, xor_and_30_and_r,
       xor_and_30_xor_r, xor_and_31_and_r, xor_and_31_xor_r, xor_and_32_and_r, xor_and_32_xor_r,
       xor_and_33_and_r, xor_and_33_xor_r, xor_and_34_and_r, xor_and_34_xor_r, xor_and_35_and_r,
       xor_and_35_xor_r, xor_and_36_and_r, xor_and_36_xor_r, xor_and_37_and_r, xor_and_37_xor_r,
       xor_and_38_and_r, xor_and_38_xor_r, xor_and_39_and_r, xor_and_39_xor_r, xor_and_40_and_r,
       xor_and_40_xor_r, xor_and_41_and_r, xor_and_41_xor_r, xor_and_42_and_r, xor_and_42_xor_r,
       xor_and_43_and_r, xor_and_43_xor_r, xor_and_44_and_r, xor_and_44_xor_r, xor_and_45_and_r,
       xor_and_45_xor_r, xor_and_46_and_r, xor_and_46_xor_r, xor_and_47_and_r, xor_and_47_xor_r,
       xor_and_48_and_r, xor_and_48_xor_r, xor_and_49_p1, xor_and_49_p2, xor_and_49_p3, xor_and_49_p4,
       xor_and_50_and_r, xor_and_50_xor_r, xor_and_51_xor_r, xor_and_52_and_r, xor_and_53_and_r,
       xor_and_53_xor_r, xor_and_54_and_r, xor_and_54_xor_r, xor_and_55_and_r, xor_and_55_xor_r,
       xor_and_56_and_r, xor_and_56_xor_r, xor_and_57_xor_r, xor_and_58_xor_r, xor_and_59_and_r,
       xor_and_59_xor_r, xor_and_60_xor_r, xor_and_61_and_r, xor_and_61_xor_r, xor_and_62_and_r,
       xor_and_62_xor_r, xor_and_63_xor_r, xor_and_64_and_r, xor_and_64_xor_r, xor_and_65_and_r,
       xor_and_65_xor_r, xor_and_66_and_r, xor_and_66_xor_r, xor_and_67_and_r, xor_and_67_xor_r,
       xor_and_68_and_r, xor_and_68_xor_r, xor_and_69_and_r, xor_and_69_xor_r, xor_and_70_and_r,
       xor_and_70_xor_r, xor_and_71_and_r, xor_and_71_xor_r, xor_and_72_and_r, xor_and_72_xor_r,
       xor_and_73_and_r, xor_and_73_xor_r, xor_and_74_and_r, xor_and_74_xor_r, xor_and_75_and_r,
       xor_and_75_xor_r, xor_and_76_and_r, xor_and_76_xor_r, xor_and_77_and_r, xor_and_77_xor_r,
       xor_and_78_and_r, xor_and_78_xor_r, xor_and_79_and_r, xor_and_79_xor_r, xor_and_80_and_r,
       xor_and_80_xor_r, xor_and_81_and_r, xor_and_81_xor_r, xor_and_82_and_r, xor_and_82_xor_r,
       xor_and_83_and_r, xor_and_83_xor_r, xor_and_84_and_r, xor_and_84_xor_r, xor_and_85_and_r,
       xor_and_85_xor_r, xor_and_86_and_r, xor_and_86_xor_r, xor_and_87_and_r, xor_and_87_xor_r,
       xor_and_88_and_r, xor_and_88_xor_r, xor_and_89_and_r, xor_and_89_xor_r, xor_and_90_and_r,
       xor_and_90_xor_r, xor_and_91_and_r, xor_and_91_xor_r, xor_and_92_and_r, xor_and_92_xor_r,
       xor_and_93_xor_r, xor_and_94_xor_r, xor_and_95_and_r, xor_and_95_xor_r, xor_and_96_xor_r,
       xor_and_97_and_r, xor_and_97_xor_r, xor_and_98_and_r, xor_and_98_xor_r, xor_and_99_xor_r,
       xor_and_100_and_r, xor_and_100_xor_r, xor_and_101_and_r, xor_and_101_xor_r, xor_and_102_and_r,
       xor_and_102_xor_r, xor_and_103_and_r, xor_and_103_xor_r, xor_and_104_and_r, xor_and_104_xor_r,
       xor_and_105_and_r, xor_and_105_xor_r, xor_and_106_and_r, xor_and_106_xor_r, xor_and_107_and_r,
       xor_and_107_xor_r, xor_and_108_and_r, xor_and_108_xor_r, xor_and_109_and_r, xor_and_109_xor_r,
       xor_and_110_and_r, xor_and_110_xor_r, xor_and_111_and_r, xor_and_111_xor_r, xor_and_112_and_r,
       xor_and_112_xor_r, xor_and_113_and_r, xor_and_113_xor_r, xor_and_114_and_r, xor_and_114_xor_r,
       xor_and_115_and_r, xor_and_115_xor_r, xor_and_116_and_r, xor_and_116_xor_r, xor_and_117_and_r,
       xor_and_117_xor_r, xor_and_118_xor_r, xor_and_119_xor_r, xor_and_120_and_r, xor_and_120_xor_r,
       xor_and_121_xor_r, xor_and_122_and_r, xor_and_122_xor_r, xor_and_123_and_r, xor_and_123_xor_r,
       xor_and_124_xor_r, xor_and_125_and_r, xor_and_125_xor_r, xor_and_126_and_r, xor_and_126_xor_r,
       xor_and_127_and_r, xor_and_127_xor_r, xor_and_128_and_r, xor_and_128_xor_r, xor_and_129_and_r,
       xor_and_129_xor_r, xor_and_130_and_r, xor_and_130_xor_r, xor_and_131_and_r, xor_and_131_xor_r,
       xor_and_132_and_r, xor_and_132_xor_r, xor_and_133_xor_r, xor_and_134_xor_r, xor_and_135_and_r,
       xor_and_135_xor_r, xor_and_136_and_r, xor_and_136_xor_r;

  xor_and xor_and_1 (.A(in_1), .B(in_9), .XOR_r(xor_and_1_xor_r), .AND_r(xor_and_1_and_r));
  xor_and xor_and_2 (.A(xor_and_3_and_r), .B(xor_and_35_xor_r), .XOR_r(xor_and_2_xor_r), .AND_r(xor_and_2_and_r));
  xor_and xor_and_3 (.A(xor_and_4_and_r), .B(xor_and_38_xor_r), .XOR_r(xor_and_3_xor_r), .AND_r(xor_and_3_and_r));
  xor_and xor_and_4 (.A(xor_and_5_and_r), .B(xor_and_6_xor_r), .XOR_r(xor_and_4_xor_r), .AND_r(xor_and_4_and_r));
  xor_and xor_and_5 (.A(xor_and_7_and_r), .B(xor_and_8_xor_r), .XOR_r(xor_and_5_xor_r), .AND_r(xor_and_5_and_r));
  xor_and xor_and_6 (.A(xor_and_8_and_r), .B(xor_and_43_xor_r), .XOR_r(xor_and_6_xor_r), .AND_r(xor_and_6_and_r));
  xor_and xor_and_7 (.A(xor_and_9_and_r), .B(xor_and_10_xor_r), .XOR_r(xor_and_7_xor_r), .AND_r(xor_and_7_and_r));
  xor_and xor_and_8 (.A(xor_and_10_and_r), .B(xor_and_46_xor_r), .XOR_r(xor_and_8_xor_r), .AND_r(xor_and_8_and_r));
  xor_and xor_and_9 (.A(xor_and_13_and_r), .B(xor_and_11_xor_r), .XOR_r(xor_and_9_xor_r), .AND_r(xor_and_9_and_r));
  xor_and xor_and_10 (.A(xor_and_11_and_r), .B(xor_and_12_xor_r), .XOR_r(xor_and_10_xor_r), .AND_r(xor_and_10_and_r));
  xor_and xor_and_11 (.A(xor_and_14_and_r), .B(xor_and_15_xor_r), .XOR_r(xor_and_11_xor_r), .AND_r(xor_and_11_and_r));
  xor_and xor_and_12 (.A(xor_and_15_and_r), .B(xor_and_51_xor_r), .XOR_r(xor_and_12_xor_r), .AND_r(xor_and_12_and_r));
  xor_and xor_and_13 (.A(xor_and_16_and_r), .B(xor_and_14_xor_r), .XOR_r(xor_and_13_xor_r), .AND_r(xor_and_13_and_r));
  xor_and xor_and_14 (.A(xor_and_17_and_r), .B(xor_and_18_xor_r), .XOR_r(xor_and_14_xor_r), .AND_r(xor_and_14_and_r));
  xor_and xor_and_15 (.A(xor_and_18_and_r), .B(xor_and_54_xor_r), .XOR_r(xor_and_15_xor_r), .AND_r(xor_and_15_and_r));
  xor_and xor_and_16 (.A(xor_and_1_and_r), .B(xor_and_17_xor_r), .XOR_r(xor_and_16_xor_r), .AND_r(xor_and_16_and_r));
  xor_and xor_and_17 (.A(in_17), .B(in_25), .XOR_r(xor_and_17_xor_r), .AND_r(xor_and_17_and_r));
  xor_and xor_and_18 (.A(in_2), .B(in_10), .XOR_r(xor_and_18_xor_r), .AND_r(xor_and_18_and_r));
  xor_and xor_and_19 (.A(xor_and_20_and_r), .B(xor_and_57_xor_r), .XOR_r(xor_and_19_xor_r));  // open: AND_r
  xor_and xor_and_20 (.A(xor_and_21_and_r), .B(xor_and_22_xor_r), .XOR_r(xor_and_20_xor_r), .AND_r(xor_and_20_and_r));
  xor_and xor_and_21 (.A(xor_and_23_and_r), .B(xor_and_24_xor_r), .XOR_r(xor_and_21_xor_r), .AND_r(xor_and_21_and_r));
  xor_and xor_and_22 (.A(xor_and_24_and_r), .B(xor_and_59_xor_r), .XOR_r(xor_and_22_xor_r), .AND_r(xor_and_22_and_r));
  xor_and xor_and_23 (.A(xor_and_25_and_r), .B(xor_and_26_xor_r), .XOR_r(xor_and_23_xor_r), .AND_r(xor_and_23_and_r));
  xor_and xor_and_24 (.A(xor_and_26_and_r), .B(xor_and_61_xor_r), .XOR_r(xor_and_24_xor_r), .AND_r(xor_and_24_and_r));
  xor_and xor_and_25 (.A(xor_and_27_and_r), .B(xor_and_28_xor_r), .XOR_r(xor_and_25_xor_r), .AND_r(xor_and_25_and_r));
  xor_and xor_and_26 (.A(xor_and_28_and_r), .B(xor_and_29_xor_r), .XOR_r(xor_and_26_xor_r), .AND_r(xor_and_26_and_r));
  xor_and xor_and_27 (.A(xor_and_30_and_r), .B(xor_and_31_xor_r), .XOR_r(xor_and_27_xor_r), .AND_r(xor_and_27_and_r));
  xor_and xor_and_28 (.A(xor_and_31_and_r), .B(xor_and_32_xor_r), .XOR_r(xor_and_28_xor_r), .AND_r(xor_and_28_and_r));
  xor_and xor_and_29 (.A(xor_and_32_and_r), .B(xor_and_66_xor_r), .XOR_r(xor_and_29_xor_r), .AND_r(xor_and_29_and_r));
  xor_and xor_and_30 (.A(xor_and_2_and_r), .B(xor_and_33_xor_r), .XOR_r(xor_and_30_xor_r), .AND_r(xor_and_30_and_r));
  xor_and xor_and_31 (.A(xor_and_33_and_r), .B(xor_and_34_xor_r), .XOR_r(xor_and_31_xor_r), .AND_r(xor_and_31_and_r));
  xor_and xor_and_32 (.A(xor_and_34_and_r), .B(xor_and_69_xor_r), .XOR_r(xor_and_32_xor_r), .AND_r(xor_and_32_and_r));
  xor_and xor_and_33 (.A(xor_and_35_and_r), .B(xor_and_36_xor_r), .XOR_r(xor_and_33_xor_r), .AND_r(xor_and_33_and_r));
  xor_and xor_and_34 (.A(xor_and_36_and_r), .B(xor_and_37_xor_r), .XOR_r(xor_and_34_xor_r), .AND_r(xor_and_34_and_r));
  xor_and xor_and_35 (.A(xor_and_38_and_r), .B(xor_and_39_xor_r), .XOR_r(xor_and_35_xor_r), .AND_r(xor_and_35_and_r));
  xor_and xor_and_36 (.A(xor_and_39_and_r), .B(xor_and_40_xor_r), .XOR_r(xor_and_36_xor_r), .AND_r(xor_and_36_and_r));
  xor_and xor_and_37 (.A(xor_and_40_and_r), .B(xor_and_74_xor_r), .XOR_r(xor_and_37_xor_r), .AND_r(xor_and_37_and_r));
  xor_and xor_and_38 (.A(xor_and_6_and_r), .B(xor_and_41_xor_r), .XOR_r(xor_and_38_xor_r), .AND_r(xor_and_38_and_r));
  xor_and xor_and_39 (.A(xor_and_41_and_r), .B(xor_and_42_xor_r), .XOR_r(xor_and_39_xor_r), .AND_r(xor_and_39_and_r));
  xor_and xor_and_40 (.A(xor_and_42_and_r), .B(xor_and_77_xor_r), .XOR_r(xor_and_40_xor_r), .AND_r(xor_and_40_and_r));
  xor_and xor_and_41 (.A(xor_and_43_and_r), .B(xor_and_44_xor_r), .XOR_r(xor_and_41_xor_r), .AND_r(xor_and_41_and_r));
  xor_and xor_and_42 (.A(xor_and_44_and_r), .B(xor_and_45_xor_r), .XOR_r(xor_and_42_xor_r), .AND_r(xor_and_42_and_r));
  xor_and xor_and_43 (.A(xor_and_46_and_r), .B(xor_and_47_xor_r), .XOR_r(xor_and_43_xor_r), .AND_r(xor_and_43_and_r));
  xor_and xor_and_44 (.A(xor_and_47_and_r), .B(xor_and_48_xor_r), .XOR_r(xor_and_44_xor_r), .AND_r(xor_and_44_and_r));
  xor_and xor_and_45 (.A(xor_and_48_and_r), .B(xor_and_82_xor_r), .XOR_r(xor_and_45_xor_r), .AND_r(xor_and_45_and_r));
  xor_and xor_and_46 (.A(xor_and_12_and_r), .B(xor_and_49_p1), .XOR_r(xor_and_46_xor_r), .AND_r(xor_and_46_and_r));
  xor_and xor_and_47 (.A(xor_and_49_p3), .B(xor_and_50_xor_r), .XOR_r(xor_and_47_xor_r), .AND_r(xor_and_47_and_r));
  xor_and xor_and_48 (.A(xor_and_50_and_r), .B(xor_and_85_xor_r), .XOR_r(xor_and_48_xor_r), .AND_r(xor_and_48_and_r));
  // xor_and xor_and_49: pin names not known; wires that end beside it: xor_and_49_p1, xor_and_49_p2, xor_and_49_p3, xor_and_49_p4
  xor_and xor_and_50 (.A(xor_and_52_and_r), .B(xor_and_53_xor_r), .XOR_r(xor_and_50_xor_r), .AND_r(xor_and_50_and_r));
  xor_and xor_and_51 (.A(xor_and_54_and_r), .B(xor_and_55_xor_r), .XOR_r(xor_and_51_xor_r), .AND_r(xor_and_49_p2));
  xor_and xor_and_52 (.A(xor_and_55_and_r), .B(xor_and_56_xor_r), .XOR_r(xor_and_49_p4), .AND_r(xor_and_52_and_r));
  xor_and xor_and_53 (.A(xor_and_56_and_r), .B(xor_and_90_xor_r), .XOR_r(xor_and_53_xor_r), .AND_r(xor_and_53_and_r));
  xor_and xor_and_54 (.A(in_18), .B(in_26), .XOR_r(xor_and_54_xor_r), .AND_r(xor_and_54_and_r));
  xor_and xor_and_55 (.A(in_3), .B(in_11), .XOR_r(xor_and_55_xor_r), .AND_r(xor_and_55_and_r));
  xor_and xor_and_56 (.A(in_19), .B(in_27), .XOR_r(xor_and_56_xor_r), .AND_r(xor_and_56_and_r));
  xor_and xor_and_57 (.A(xor_and_22_and_r), .B(xor_and_58_xor_r), .XOR_r(xor_and_57_xor_r));  // open: AND_r
  xor_and xor_and_58 (.A(xor_and_59_and_r), .B(xor_and_60_xor_r), .XOR_r(xor_and_58_xor_r));  // open: AND_r
  xor_and xor_and_59 (.A(xor_and_61_and_r), .B(xor_and_62_xor_r), .XOR_r(xor_and_59_xor_r), .AND_r(xor_and_59_and_r));
  xor_and xor_and_60 (.A(xor_and_62_and_r), .B(xor_and_63_xor_r), .XOR_r(xor_and_60_xor_r));  // open: AND_r
  xor_and xor_and_61 (.A(xor_and_29_and_r), .B(xor_and_64_xor_r), .XOR_r(xor_and_61_xor_r), .AND_r(xor_and_61_and_r));
  xor_and xor_and_62 (.A(xor_and_64_and_r), .B(xor_and_65_xor_r), .XOR_r(xor_and_62_xor_r), .AND_r(xor_and_62_and_r));
  xor_and xor_and_63 (.A(xor_and_65_and_r), .B(xor_and_93_xor_r), .XOR_r(xor_and_63_xor_r));  // open: AND_r
  xor_and xor_and_64 (.A(xor_and_66_and_r), .B(xor_and_67_xor_r), .XOR_r(xor_and_64_xor_r), .AND_r(xor_and_64_and_r));
  xor_and xor_and_65 (.A(xor_and_67_and_r), .B(xor_and_68_xor_r), .XOR_r(xor_and_65_xor_r), .AND_r(xor_and_65_and_r));
  xor_and xor_and_66 (.A(xor_and_69_and_r), .B(xor_and_70_xor_r), .XOR_r(xor_and_66_xor_r), .AND_r(xor_and_66_and_r));
  xor_and xor_and_67 (.A(xor_and_70_and_r), .B(xor_and_71_xor_r), .XOR_r(xor_and_67_xor_r), .AND_r(xor_and_67_and_r));
  xor_and xor_and_68 (.A(xor_and_71_and_r), .B(xor_and_95_xor_r), .XOR_r(xor_and_68_xor_r), .AND_r(xor_and_68_and_r));
  xor_and xor_and_69 (.A(xor_and_37_and_r), .B(xor_and_72_xor_r), .XOR_r(xor_and_69_xor_r), .AND_r(xor_and_69_and_r));
  xor_and xor_and_70 (.A(xor_and_72_and_r), .B(xor_and_73_xor_r), .XOR_r(xor_and_70_xor_r), .AND_r(xor_and_70_and_r));
  xor_and xor_and_71 (.A(xor_and_73_and_r), .B(xor_and_97_xor_r), .XOR_r(xor_and_71_xor_r), .AND_r(xor_and_71_and_r));
  xor_and xor_and_72 (.A(xor_and_74_and_r), .B(xor_and_75_xor_r), .XOR_r(xor_and_72_xor_r), .AND_r(xor_and_72_and_r));
  xor_and xor_and_73 (.A(xor_and_75_and_r), .B(xor_and_76_xor_r), .XOR_r(xor_and_73_xor_r), .AND_r(xor_and_73_and_r));
  xor_and xor_and_74 (.A(xor_and_77_and_r), .B(xor_and_78_xor_r), .XOR_r(xor_and_74_xor_r), .AND_r(xor_and_74_and_r));
  xor_and xor_and_75 (.A(xor_and_78_and_r), .B(xor_and_79_xor_r), .XOR_r(xor_and_75_xor_r), .AND_r(xor_and_75_and_r));
  xor_and xor_and_76 (.A(xor_and_79_and_r), .B(xor_and_102_xor_r), .XOR_r(xor_and_76_xor_r), .AND_r(xor_and_76_and_r));
  xor_and xor_and_77 (.A(xor_and_45_and_r), .B(xor_and_80_xor_r), .XOR_r(xor_and_77_xor_r), .AND_r(xor_and_77_and_r));
  xor_and xor_and_78 (.A(xor_and_80_and_r), .B(xor_and_81_xor_r), .XOR_r(xor_and_78_xor_r), .AND_r(xor_and_78_and_r));
  xor_and xor_and_79 (.A(xor_and_81_and_r), .B(xor_and_105_xor_r), .XOR_r(xor_and_79_xor_r), .AND_r(xor_and_79_and_r));
  xor_and xor_and_80 (.A(xor_and_82_and_r), .B(xor_and_83_xor_r), .XOR_r(xor_and_80_xor_r), .AND_r(xor_and_80_and_r));
  xor_and xor_and_81 (.A(xor_and_83_and_r), .B(xor_and_84_xor_r), .XOR_r(xor_and_81_xor_r), .AND_r(xor_and_81_and_r));
  xor_and xor_and_82 (.A(xor_and_85_and_r), .B(xor_and_86_xor_r), .XOR_r(xor_and_82_xor_r), .AND_r(xor_and_82_and_r));
  xor_and xor_and_83 (.A(xor_and_86_and_r), .B(xor_and_87_xor_r), .XOR_r(xor_and_83_xor_r), .AND_r(xor_and_83_and_r));
  xor_and xor_and_84 (.A(xor_and_87_and_r), .B(xor_and_110_xor_r), .XOR_r(xor_and_84_xor_r), .AND_r(xor_and_84_and_r));
  xor_and xor_and_85 (.A(xor_and_53_and_r), .B(xor_and_88_xor_r), .XOR_r(xor_and_85_xor_r), .AND_r(xor_and_85_and_r));
  xor_and xor_and_86 (.A(xor_and_88_and_r), .B(xor_and_89_xor_r), .XOR_r(xor_and_86_xor_r), .AND_r(xor_and_86_and_r));
  xor_and xor_and_87 (.A(xor_and_89_and_r), .B(xor_and_113_xor_r), .XOR_r(xor_and_87_xor_r), .AND_r(xor_and_87_and_r));
  xor_and xor_and_88 (.A(xor_and_90_and_r), .B(xor_and_91_xor_r), .XOR_r(xor_and_88_xor_r), .AND_r(xor_and_88_and_r));
  xor_and xor_and_89 (.A(xor_and_91_and_r), .B(xor_and_92_xor_r), .XOR_r(xor_and_89_xor_r), .AND_r(xor_and_89_and_r));
  xor_and xor_and_90 (.A(in_4), .B(in_12), .XOR_r(xor_and_90_xor_r), .AND_r(xor_and_90_and_r));
  xor_and xor_and_91 (.A(in_20), .B(in_28), .XOR_r(xor_and_91_xor_r), .AND_r(xor_and_91_and_r));
  xor_and xor_and_92 (.A(in_5), .B(in_13), .XOR_r(xor_and_92_xor_r), .AND_r(xor_and_92_and_r));
  xor_and xor_and_93 (.A(xor_and_68_and_r), .B(xor_and_94_xor_r), .XOR_r(xor_and_93_xor_r));  // open: AND_r
  xor_and xor_and_94 (.A(xor_and_95_and_r), .B(xor_and_96_xor_r), .XOR_r(xor_and_94_xor_r));  // open: AND_r
  xor_and xor_and_95 (.A(xor_and_97_and_r), .B(xor_and_98_xor_r), .XOR_r(xor_and_95_xor_r), .AND_r(xor_and_95_and_r));
  xor_and xor_and_96 (.A(xor_and_98_and_r), .B(xor_and_99_xor_r), .XOR_r(xor_and_96_xor_r));  // open: AND_r
  xor_and xor_and_97 (.A(xor_and_76_and_r), .B(xor_and_100_xor_r), .XOR_r(xor_and_97_xor_r), .AND_r(xor_and_97_and_r));
  xor_and xor_and_98 (.A(xor_and_100_and_r), .B(xor_and_101_xor_r), .XOR_r(xor_and_98_xor_r), .AND_r(xor_and_98_and_r));
  xor_and xor_and_99 (.A(xor_and_101_and_r), .B(xor_and_118_xor_r), .XOR_r(xor_and_99_xor_r));  // open: AND_r
  xor_and xor_and_100 (
    .A(xor_and_102_and_r), .B(xor_and_103_xor_r), .XOR_r(xor_and_100_xor_r), .AND_r(xor_and_100_and_r));
  xor_and xor_and_101 (
    .A(xor_and_103_and_r), .B(xor_and_104_xor_r), .XOR_r(xor_and_101_xor_r), .AND_r(xor_and_101_and_r));
  xor_and xor_and_102 (
    .A(xor_and_105_and_r), .B(xor_and_106_xor_r), .XOR_r(xor_and_102_xor_r), .AND_r(xor_and_102_and_r));
  xor_and xor_and_103 (
    .A(xor_and_106_and_r), .B(xor_and_107_xor_r), .XOR_r(xor_and_103_xor_r), .AND_r(xor_and_103_and_r));
  xor_and xor_and_104 (
    .A(xor_and_107_and_r), .B(xor_and_120_xor_r), .XOR_r(xor_and_104_xor_r), .AND_r(xor_and_104_and_r));
  xor_and xor_and_105 (
    .A(xor_and_84_and_r), .B(xor_and_108_xor_r), .XOR_r(xor_and_105_xor_r), .AND_r(xor_and_105_and_r));
  xor_and xor_and_106 (
    .A(xor_and_108_and_r), .B(xor_and_109_xor_r), .XOR_r(xor_and_106_xor_r), .AND_r(xor_and_106_and_r));
  xor_and xor_and_107 (
    .A(xor_and_109_and_r), .B(xor_and_122_xor_r), .XOR_r(xor_and_107_xor_r), .AND_r(xor_and_107_and_r));
  xor_and xor_and_108 (
    .A(xor_and_110_and_r), .B(xor_and_111_xor_r), .XOR_r(xor_and_108_xor_r), .AND_r(xor_and_108_and_r));
  xor_and xor_and_109 (
    .A(xor_and_111_and_r), .B(xor_and_112_xor_r), .XOR_r(xor_and_109_xor_r), .AND_r(xor_and_109_and_r));
  xor_and xor_and_110 (
    .A(xor_and_113_and_r), .B(xor_and_114_xor_r), .XOR_r(xor_and_110_xor_r), .AND_r(xor_and_110_and_r));
  xor_and xor_and_111 (
    .A(xor_and_114_and_r), .B(xor_and_115_xor_r), .XOR_r(xor_and_111_xor_r), .AND_r(xor_and_111_and_r));
  xor_and xor_and_112 (
    .A(xor_and_115_and_r), .B(xor_and_127_xor_r), .XOR_r(xor_and_112_xor_r), .AND_r(xor_and_112_and_r));
  xor_and xor_and_113 (
    .A(xor_and_92_and_r), .B(xor_and_116_xor_r), .XOR_r(xor_and_113_xor_r), .AND_r(xor_and_113_and_r));
  xor_and xor_and_114 (
    .A(xor_and_116_and_r), .B(xor_and_117_xor_r), .XOR_r(xor_and_114_xor_r), .AND_r(xor_and_114_and_r));
  xor_and xor_and_115 (
    .A(xor_and_117_and_r), .B(xor_and_130_xor_r), .XOR_r(xor_and_115_xor_r), .AND_r(xor_and_115_and_r));
  xor_and xor_and_116 (.A(in_21), .B(in_29), .XOR_r(xor_and_116_xor_r), .AND_r(xor_and_116_and_r));
  xor_and xor_and_117 (.A(in_6), .B(in_14), .XOR_r(xor_and_117_xor_r), .AND_r(xor_and_117_and_r));
  xor_and xor_and_118 (.A(xor_and_104_and_r), .B(xor_and_119_xor_r), .XOR_r(xor_and_118_xor_r));  // open: AND_r
  xor_and xor_and_119 (.A(xor_and_120_and_r), .B(xor_and_121_xor_r), .XOR_r(xor_and_119_xor_r));  // open: AND_r
  xor_and xor_and_120 (
    .A(xor_and_122_and_r), .B(xor_and_123_xor_r), .XOR_r(xor_and_120_xor_r), .AND_r(xor_and_120_and_r));
  xor_and xor_and_121 (.A(xor_and_123_and_r), .B(xor_and_124_xor_r), .XOR_r(xor_and_121_xor_r));  // open: AND_r
  xor_and xor_and_122 (
    .A(xor_and_112_and_r), .B(xor_and_125_xor_r), .XOR_r(xor_and_122_xor_r), .AND_r(xor_and_122_and_r));
  xor_and xor_and_123 (
    .A(xor_and_125_and_r), .B(xor_and_126_xor_r), .XOR_r(xor_and_123_xor_r), .AND_r(xor_and_123_and_r));
  xor_and xor_and_124 (.A(xor_and_126_and_r), .B(xor_and_133_xor_r), .XOR_r(xor_and_124_xor_r));  // open: AND_r
  xor_and xor_and_125 (
    .A(xor_and_127_and_r), .B(xor_and_128_xor_r), .XOR_r(xor_and_125_xor_r), .AND_r(xor_and_125_and_r));
  xor_and xor_and_126 (
    .A(xor_and_128_and_r), .B(xor_and_129_xor_r), .XOR_r(xor_and_126_xor_r), .AND_r(xor_and_126_and_r));
  xor_and xor_and_127 (
    .A(xor_and_130_and_r), .B(xor_and_131_xor_r), .XOR_r(xor_and_127_xor_r), .AND_r(xor_and_127_and_r));
  xor_and xor_and_128 (
    .A(xor_and_131_and_r), .B(xor_and_132_xor_r), .XOR_r(xor_and_128_xor_r), .AND_r(xor_and_128_and_r));
  xor_and xor_and_129 (
    .A(xor_and_132_and_r), .B(xor_and_135_xor_r), .XOR_r(xor_and_129_xor_r), .AND_r(xor_and_129_and_r));
  xor_and xor_and_130 (.A(in_22), .B(in_30), .XOR_r(xor_and_130_xor_r), .AND_r(xor_and_130_and_r));
  xor_and xor_and_131 (.A(in_7), .B(in_15), .XOR_r(xor_and_131_xor_r), .AND_r(xor_and_131_and_r));
  xor_and xor_and_132 (.A(in_23), .B(in_31), .XOR_r(xor_and_132_xor_r), .AND_r(xor_and_132_and_r));
  xor_and xor_and_133 (.A(xor_and_129_and_r), .B(xor_and_134_xor_r), .XOR_r(xor_and_133_xor_r));  // open: AND_r
  xor_and xor_and_134 (.A(xor_and_135_and_r), .B(xor_and_136_xor_r), .XOR_r(xor_and_134_xor_r));  // open: AND_r
  xor_and xor_and_135 (.A(in_8), .B(in_16), .XOR_r(xor_and_135_xor_r), .AND_r(xor_and_135_and_r));
  xor_and xor_and_136 (.A(in_24), .B(in_32), .XOR_r(xor_and_136_xor_r), .AND_r(xor_and_136_and_r));
endmodule

module or_8_inputs (
  input  in_1,
  input  in_2,
  input  in_3,
  input  in_4,
  input  in_5,
  input  in_6,
  input  in_7,
  input  in_8,
  output out_9
);

  wire or_2_out, or_3_out, or_4_out, or_5_out, or_6_out, or_7_out;

  or or_1 (out_9, or_2_out, or_5_out);
  or or_2 (or_2_out, or_3_out, or_4_out);
  or or_3 (or_3_out, in_1, in_2);
  or or_4 (or_4_out, in_3, in_4);
  or or_5 (or_5_out, or_6_out, or_7_out);
  or or_6 (or_6_out, in_5, in_6);
  or or_7 (or_7_out, in_7, in_8);
endmodule

module multiplying_module (
  input  B1I,
  input  B2I,
  input  B3I,
  input  B4I,
  input  B5I,
  input  B6I,
  input  B7I,
  input  B8I,
  input  B1T,
  input  B2T,
  input  B3T,
  input  B4T,
  input  B5T,
  input  B6T,
  input  B7T,
  input  B8T,
  output B2O,
  output B4O,
  output B6O,
  output B8O,
  output B1O,
  output B3O,
  output B50,
  output B70,
  output ERR
);

  wire adding_module_1_b1o, adding_module_1_b2o, adding_module_1_b3o, adding_module_1_b4o,
       adding_module_1_b5o, adding_module_1_b6o, adding_module_1_b7o, adding_module_1_b8o,
       adding_module_1_error, adding_module_2_b1o, adding_module_2_b2o, adding_module_2_b3o,
       adding_module_2_b4o, adding_module_2_b5o, adding_module_2_b6o, adding_module_2_b7o,
       adding_module_2_b8o, adding_module_2_error, adding_module_3_error, adding_module_4_b1o,
       adding_module_4_b2o, adding_module_4_b3o, adding_module_4_b4o, adding_module_4_b5o,
       adding_module_4_b6o, adding_module_4_b7o, adding_module_4_b8o, adding_module_4_error,
       adding_module_5_b1o, adding_module_5_b2o, adding_module_5_b3o, adding_module_5_b4o,
       adding_module_5_b5o, adding_module_5_b6o, adding_module_5_b7o, adding_module_5_b8o,
       adding_module_5_error, adding_module_6_b1o, adding_module_6_b2o, adding_module_6_b3o,
       adding_module_6_b4o, adding_module_6_b5o, adding_module_6_b6o, adding_module_6_b7o,
       adding_module_6_b8o, adding_module_6_error, adding_module_7_b1o, adding_module_7_b2o,
       adding_module_7_b3o, adding_module_7_b4o, adding_module_7_b5o, adding_module_7_b6o,
       adding_module_7_b7o, adding_module_7_b8o, adding_module_7_error, multiy_component_1_b1o,
       multiy_component_1_b2o, multiy_component_1_b3o, multiy_component_1_b4o, multiy_component_1_b5o,
       multiy_component_1_b6o, multiy_component_1_b7o, multiy_component_1_b8o, multiy_component_2_b1o,
       multiy_component_2_b2o, multiy_component_2_b3o, multiy_component_2_b4o, multiy_component_2_b5o,
       multiy_component_2_b6o, multiy_component_2_b7o, multiy_component_2_b8o, multiy_component_3_b1o,
       multiy_component_3_b2o, multiy_component_3_b3o, multiy_component_3_b4o, multiy_component_3_b5o,
       multiy_component_3_b6o, multiy_component_3_b7o, multiy_component_3_b8o, multiy_component_4_b1o,
       multiy_component_4_b2o, multiy_component_4_b3o, multiy_component_4_b4o, multiy_component_4_b5o,
       multiy_component_4_b6o, multiy_component_4_b7o, multiy_component_4_b8o, multiy_component_5_b1o,
       multiy_component_5_b2o, multiy_component_5_b3o, multiy_component_5_b4o, multiy_component_5_b5o,
       multiy_component_5_b6o, multiy_component_5_b7o, multiy_component_5_b8o, multiy_component_6_b1o,
       multiy_component_6_b2o, multiy_component_6_b3o, multiy_component_6_b4o, multiy_component_6_b5o,
       multiy_component_6_b6o, multiy_component_6_b7o, multiy_component_6_b8o, multiy_component_7_b1o,
       multiy_component_7_b2o, multiy_component_7_b3o, multiy_component_7_b4o, multiy_component_7_b5o,
       multiy_component_7_b6o, multiy_component_7_b7o, multiy_component_7_b8o, multiy_component_8_b1o,
       multiy_component_8_b2o, multiy_component_8_b3o, multiy_component_8_b4o, multiy_component_8_b5o,
       multiy_component_8_b6o, multiy_component_8_b7o, multiy_component_8_b8o, or_1_out, or_2_out, or_3_out,
       or_8_inputs_2_out_9, or_8_inputs_3_out_9, or_8_inputs_4_out_9, or_8_inputs_5_out_9, undriven;

  adding_module adding_module_1 (
    .B5F(adding_module_2_b5o), .B6F(adding_module_2_b6o), .B7F(adding_module_2_b7o),
    .B8F(adding_module_2_b8o), .B3S(multiy_component_3_b1o), .B4S(multiy_component_3_b2o),
    .B5S(multiy_component_3_b3o), .B6S(multiy_component_3_b4o), .B7S(multiy_component_3_b5o),
    .B8S(multiy_component_3_b6o), .B1F(adding_module_2_b1o), .B2F(adding_module_2_b2o),
    .B3F(adding_module_2_b3o), .B4F(adding_module_2_b4o), .B1O(adding_module_1_b1o),
    .B2O(adding_module_1_b2o), .B3O(adding_module_1_b3o), .B4O(adding_module_1_b4o),
    .B5O(adding_module_1_b5o), .B6O(adding_module_1_b6o), .B7O(adding_module_1_b7o),
    .B8O(adding_module_1_b8o), .ERROR(adding_module_1_error));  // open: B1S, B2S
  adding_module adding_module_2 (
    .B5F(multiy_component_1_b5o), .B6F(multiy_component_1_b6o), .B7F(multiy_component_1_b7o),
    .B8F(multiy_component_1_b8o), .B2S(multiy_component_2_b1o), .B3S(multiy_component_2_b2o),
    .B4S(multiy_component_2_b3o), .B5S(multiy_component_2_b4o), .B6S(multiy_component_2_b5o),
    .B7S(multiy_component_2_b6o), .B8S(multiy_component_2_b7o), .B1F(multiy_component_1_b1o),
    .B2F(multiy_component_1_b2o), .B3F(multiy_component_1_b3o), .B4F(multiy_component_1_b4o),
    .B1O(adding_module_2_b1o), .B2O(adding_module_2_b2o), .B3O(adding_module_2_b3o),
    .B4O(adding_module_2_b4o), .B5O(adding_module_2_b5o), .B6O(adding_module_2_b6o),
    .B7O(adding_module_2_b7o), .B8O(adding_module_2_b8o), .ERROR(adding_module_2_error));  // open: B1S
  multiy_component multiy_component_1 (
    .b1o(multiy_component_1_b1o), .b2o(multiy_component_1_b2o), .b3o(multiy_component_1_b3o),
    .b4o(multiy_component_1_b4o), .b5o(multiy_component_1_b5o), .b6o(multiy_component_1_b6o),
    .b7o(multiy_component_1_b7o), .b8o(multiy_component_1_b8o), .Mno(undriven), .b1(B1T), .b2(B2T), .b3(B3T),
    .b4(B4T), .b5(B5T), .b6(B6T), .b7(B7T), .b8(B8T));
  multiy_component multiy_component_2 (
    .b1o(multiy_component_2_b1o), .b2o(multiy_component_2_b2o), .b3o(multiy_component_2_b3o),
    .b4o(multiy_component_2_b4o), .b5o(multiy_component_2_b5o), .b6o(multiy_component_2_b6o),
    .b7o(multiy_component_2_b7o), .b8o(multiy_component_2_b8o), .Mno(B2I), .b1(B1T), .b2(B2T), .b3(B3T),
    .b4(B4T), .b5(B5T), .b6(B6T), .b7(B7T), .b8(B8T));
  or_8_inputs or_8_inputs_1 (
    .out_9(ERR), .in_1(adding_module_2_error), .in_2(adding_module_1_error), .in_3(adding_module_7_error),
    .in_4(adding_module_6_error), .in_5(adding_module_5_error), .in_6(adding_module_4_error),
    .in_7(adding_module_3_error), .in_8(or_1_out));
  multiy_component multiy_component_3 (
    .b1o(multiy_component_3_b1o), .b2o(multiy_component_3_b2o), .b3o(multiy_component_3_b3o),
    .b4o(multiy_component_3_b4o), .b5o(multiy_component_3_b5o), .b6o(multiy_component_3_b6o),
    .b7o(multiy_component_3_b7o), .b8o(multiy_component_3_b8o), .Mno(B3I), .b1(B1T), .b2(B2T), .b3(B3T),
    .b4(B4T), .b5(B5T), .b6(B6T), .b7(B7T), .b8(B8T));
  adding_module adding_module_3 (
    .B5F(adding_module_4_b5o), .B6F(adding_module_4_b6o), .B7F(adding_module_4_b7o),
    .B8F(adding_module_4_b8o), .B8S(multiy_component_8_b1o), .B1F(adding_module_4_b1o),
    .B2F(adding_module_4_b2o), .B3F(adding_module_4_b3o), .B4F(adding_module_4_b4o), .B1O(B1O), .B2O(B2O),
    .B3O(B3O), .B4O(B4O), .B5O(B50), .B6O(B6O), .B7O(B70), .B8O(B8O), .ERROR(adding_module_3_error));  // open: B1S, B2S, B3S, B4S, B5S, B6S, B7S
  adding_module adding_module_4 (
    .B5F(adding_module_5_b5o), .B6F(adding_module_5_b6o), .B7F(adding_module_5_b7o),
    .B8F(adding_module_5_b8o), .B7S(multiy_component_7_b1o), .B8S(multiy_component_7_b2o),
    .B1F(adding_module_5_b1o), .B2F(adding_module_5_b2o), .B3F(adding_module_5_b3o),
    .B4F(adding_module_5_b4o), .B1O(adding_module_4_b1o), .B2O(adding_module_4_b2o),
    .B3O(adding_module_4_b3o), .B4O(adding_module_4_b4o), .B5O(adding_module_4_b5o),
    .B6O(adding_module_4_b6o), .B7O(adding_module_4_b7o), .B8O(adding_module_4_b8o),
    .ERROR(adding_module_4_error));  // open: B1S, B2S, B3S, B4S, B5S, B6S
  adding_module adding_module_5 (
    .B5F(adding_module_6_b5o), .B6F(adding_module_6_b6o), .B7F(adding_module_6_b7o),
    .B8F(adding_module_6_b8o), .B6S(multiy_component_6_b1o), .B7S(multiy_component_6_b2o),
    .B8S(multiy_component_6_b3o), .B1F(adding_module_6_b1o), .B2F(adding_module_6_b2o),
    .B3F(adding_module_6_b3o), .B4F(adding_module_6_b4o), .B1O(adding_module_5_b1o),
    .B2O(adding_module_5_b2o), .B3O(adding_module_5_b3o), .B4O(adding_module_5_b4o),
    .B5O(adding_module_5_b5o), .B6O(adding_module_5_b6o), .B7O(adding_module_5_b7o),
    .B8O(adding_module_5_b8o), .ERROR(adding_module_5_error));  // open: B1S, B2S, B3S, B4S, B5S
  adding_module adding_module_6 (
    .B5F(adding_module_7_b5o), .B6F(adding_module_7_b6o), .B7F(adding_module_7_b7o),
    .B8F(adding_module_7_b8o), .B5S(multiy_component_5_b1o), .B6S(multiy_component_5_b2o),
    .B7S(multiy_component_5_b3o), .B8S(multiy_component_5_b4o), .B1F(adding_module_7_b1o),
    .B2F(adding_module_7_b2o), .B3F(adding_module_7_b3o), .B4F(adding_module_7_b4o),
    .B1O(adding_module_6_b1o), .B2O(adding_module_6_b2o), .B3O(adding_module_6_b3o),
    .B4O(adding_module_6_b4o), .B5O(adding_module_6_b5o), .B6O(adding_module_6_b6o),
    .B7O(adding_module_6_b7o), .B8O(adding_module_6_b8o), .ERROR(adding_module_6_error));  // open: B1S, B2S, B3S, B4S
  adding_module adding_module_7 (
    .B5F(adding_module_1_b5o), .B6F(adding_module_1_b6o), .B7F(adding_module_1_b7o),
    .B8F(adding_module_1_b8o), .B4S(multiy_component_4_b1o), .B5S(multiy_component_4_b2o),
    .B6S(multiy_component_4_b3o), .B7S(multiy_component_4_b4o), .B8S(multiy_component_4_b5o),
    .B1F(adding_module_1_b1o), .B2F(adding_module_1_b2o), .B3F(adding_module_1_b3o),
    .B4F(adding_module_1_b4o), .B1O(adding_module_7_b1o), .B2O(adding_module_7_b2o),
    .B3O(adding_module_7_b3o), .B4O(adding_module_7_b4o), .B5O(adding_module_7_b5o),
    .B6O(adding_module_7_b6o), .B7O(adding_module_7_b7o), .B8O(adding_module_7_b8o),
    .ERROR(adding_module_7_error));  // open: B1S, B2S, B3S
  multiy_component multiy_component_4 (
    .b1o(multiy_component_4_b1o), .b2o(multiy_component_4_b2o), .b3o(multiy_component_4_b3o),
    .b4o(multiy_component_4_b4o), .b5o(multiy_component_4_b5o), .b6o(multiy_component_4_b6o),
    .b7o(multiy_component_4_b7o), .b8o(multiy_component_4_b8o), .Mno(B4I), .b1(B1T), .b2(B2T), .b3(B3T),
    .b4(B4T), .b5(B5T), .b6(B6T), .b7(B7T), .b8(B8T));
  multiy_component multiy_component_5 (
    .b1o(multiy_component_5_b1o), .b2o(multiy_component_5_b2o), .b3o(multiy_component_5_b3o),
    .b4o(multiy_component_5_b4o), .b5o(multiy_component_5_b5o), .b6o(multiy_component_5_b6o),
    .b7o(multiy_component_5_b7o), .b8o(multiy_component_5_b8o), .Mno(B5I), .b1(B1T), .b2(B2T), .b3(B3T),
    .b4(B4T), .b5(B5T), .b6(B6T), .b7(B7T), .b8(B8T));
  multiy_component multiy_component_6 (
    .b1o(multiy_component_6_b1o), .b2o(multiy_component_6_b2o), .b3o(multiy_component_6_b3o),
    .b4o(multiy_component_6_b4o), .b5o(multiy_component_6_b5o), .b6o(multiy_component_6_b6o),
    .b7o(multiy_component_6_b7o), .b8o(multiy_component_6_b8o), .Mno(B6I), .b1(B1T), .b2(B2T), .b3(B3T),
    .b4(B4T), .b5(B5T), .b6(B6T), .b7(B7T), .b8(B8T));
  or or_1 (or_1_out, or_8_inputs_2_out_9, or_2_out);
  multiy_component multiy_component_7 (
    .b1o(multiy_component_7_b1o), .b2o(multiy_component_7_b2o), .b3o(multiy_component_7_b3o),
    .b4o(multiy_component_7_b4o), .b5o(multiy_component_7_b5o), .b6o(multiy_component_7_b6o),
    .b7o(multiy_component_7_b7o), .b8o(multiy_component_7_b8o), .Mno(B7I), .b1(B1T), .b2(B2T), .b3(B3T),
    .b4(B4T), .b5(B5T), .b6(B6T), .b7(B7T), .b8(B8T));
  or_8_inputs or_8_inputs_2 (
    .out_9(or_8_inputs_2_out_9), .in_1(multiy_component_5_b7o), .in_2(multiy_component_5_b8o),
    .in_3(multiy_component_6_b4o), .in_4(multiy_component_6_b5o), .in_5(multiy_component_6_b6o),
    .in_6(multiy_component_6_b7o), .in_7(multiy_component_6_b8o), .in_8(multiy_component_7_b3o));
  or_8_inputs or_8_inputs_3 (
    .out_9(or_8_inputs_3_out_9), .in_1(multiy_component_2_b8o), .in_2(multiy_component_3_b7o),
    .in_3(multiy_component_3_b8o), .in_4(multiy_component_4_b6o), .in_5(multiy_component_4_b7o),
    .in_6(multiy_component_4_b8o), .in_7(multiy_component_5_b5o), .in_8(multiy_component_5_b6o));
  multiy_component multiy_component_8 (
    .b1o(multiy_component_8_b1o), .b2o(multiy_component_8_b2o), .b3o(multiy_component_8_b3o),
    .b4o(multiy_component_8_b4o), .b5o(multiy_component_8_b5o), .b6o(multiy_component_8_b6o),
    .b7o(multiy_component_8_b7o), .b8o(multiy_component_8_b8o), .Mno(B8I), .b1(B1T), .b2(B2T), .b3(B3T),
    .b4(B4T), .b5(B5T), .b6(B6T), .b7(B7T), .b8(B8T));
  or or_2 (or_2_out, or_8_inputs_3_out_9, or_3_out);
  or_8_inputs or_8_inputs_4 (
    .out_9(or_8_inputs_4_out_9), .in_1(multiy_component_8_b5o), .in_2(multiy_component_8_b6o),
    .in_3(multiy_component_8_b7o), .in_4(multiy_component_8_b8o));  // open: in_5, in_6, in_7, in_8
  or or_3 (or_3_out, or_8_inputs_5_out_9, or_8_inputs_4_out_9);
  or_8_inputs or_8_inputs_5 (
    .out_9(or_8_inputs_5_out_9), .in_1(multiy_component_7_b4o), .in_2(multiy_component_7_b5o),
    .in_3(multiy_component_7_b6o), .in_4(multiy_component_7_b7o), .in_5(multiy_component_7_b8o),
    .in_6(multiy_component_8_b2o), .in_7(multiy_component_8_b3o), .in_8(multiy_component_8_b4o));
endmodule

module compere_equal (
  input  b1f,
  input  b1s,
  input  b2f,
  input  b2s,
  input  b3f,
  input  b3s,
  input  b4f,
  input  b4s,
  input  b5f,
  input  b5s,
  input  b6f,
  input  b6s,
  input  b7f,
  input  b7s,
  input  b8f,
  input  b8s,
  output Equal
);

  wire and_1_out, and_2_out, and_3_out, and_4_out, and_5_out, and_6_out, and_7_out, and_8_out, and_9_out,
       and_10_out, and_11_out, and_12_out, and_13_out, and_14_out;

  and and_1 (and_1_out, b1f, b1s);
  and and_2 (and_2_out, b2f, b2s);
  and and_3 (and_3_out, b3f, b3s);
  and and_4 (and_4_out, b4f, b4s);
  and and_5 (and_5_out, b5f, b5s);
  and and_6 (and_6_out, b6f, b6s);
  and and_7 (and_7_out, b7f, b7s);
  and and_8 (and_8_out, b8f, b8s);
  and and_9 (and_9_out, and_1_out, and_2_out);
  and and_10 (and_10_out, and_9_out, and_11_out);
  and and_11 (and_11_out, and_3_out, and_4_out);
  and and_12 (and_12_out, and_5_out, and_6_out);
  and and_13 (and_13_out, and_12_out, and_14_out);
  and and_14 (and_14_out, and_7_out, and_8_out);
  and and_15 (Equal, and_10_out, and_13_out);
endmodule

module compering_module (
  input  B1,
  input  B2,
  output B1_is_greater,
  output B2_is_greater,
  output Equal
);

  and and_1 (Equal, B1, B2);
  buf xor_1 (B1_is_greater, B1);  // XOR_Gate
  buf xor_2 (B2_is_greater, B2);  // XOR_Gate
endmodule
